# Fritzing sketch Angad uno pcb design (saved by Fritzing 1.0.1rc)
circuit board: 5.97568cm x 3.48716cm
stripboards: 1

parts:
  Power_plug3 = Power plug
  J10 = female pin header, 6 pins [form="♀ (female rounded)"]
  J10_2 = female pin header, 4 pins [form="♀ (female rounded)"]
  J12 = female pin header, 5 pins [form="♀ (female rounded)"]
  J13 = female pin header, 6 pins [form="♀ (female rounded)"]
  U5 = Voltage Regulator - 5V [package="DPak [SMD]"]
  S4 = Pushbutton [package="[SMD]"]
  R4 = Resistor [tolerance=±5% resistance=1k package="0805 [SMD]"]
  D3 = Rectifier Diode [part_number=1N4001 package="Melf DO-213 AB [SMD]"]
  C10 = Ceramic Capacitor [capacitance=22pF package="0805 [SMD, multilayer]"]
  C11 = Ceramic Capacitor [capacitance=22pF package="0805 [SMD, multilayer]"]
  C10_2 = Electrolytic Capacitor [capacitance=47µF package="1010 [SMD, electrolytic]"]
  C10_3 = Electrolytic Capacitor [capacitance=1µF package="0807 [SMD, electrolytic]"]
  C12 = Ceramic Capacitor [capacitance=100nF package="0805 [SMD, multilayer]"]
  ICSP = female pin header, 6 pins [form="♀ (female rounded)"]
  U6 = atmega168 [package=dip]
  XTAL3 = Crystal [frequency="16 Mhz" package=SMD]

nets:
  GND: Power_plug3.GND, U5.GND, S4.Pin_3, S4.Pin_4, C10.0, C11.1, C10_2.-, C10_3.-, ICSP.pin5, ICSP.pin6, U6.GND
  N1: Power_plug3.VCC, D3.anode
  N2: J10.pin1, S4.Pin_1, S4.Pin_2, R4.Pin_0, C12.1, U6.RESET
  N3: J10.pin2, ICSP.pin3, U6.D0_(RX)
  N4: J10.pin3, ICSP.pin2, U6.D1_(TX)
  N5: J10.pin4, U6.D2
  N6: J10.pin5, U6.D3_(PWM)
  N7: J10.pin6, U6.D4
  N8: J10_2.pin1, U6.D5_(PWM)
  N9: J10_2.pin2, U6.D6_(PWM)
  N10: J10_2.pin3, U6.D7
  N11: J10_2.pin4, U6.D8
  N12: J12.pin1, U6.D13
  N13: J12.pin2, U6.D12
  N14: J12.pin3, U6.D11_(PWM)
  N15: J12.pin4, U6.D10_(PWM)
  N16: J12.pin5, U6.D9_(PWM)
  N17: J13.pin1, U6.A5
  N18: J13.pin2, U6.A4
  N19: J13.pin3, U6.A3
  N20: J13.pin4, U6.A2
  N21: J13.pin5, U6.A1
  N22: J13.pin6, U6.A0
  N23: U5.input_voltage, D3.cathode, C10_2.+
  N24: U5.output_voltage, R4.Pin_1, C10_3.+, ICSP.pin4, U6.VCC, U6.AVCC, U6.AREF
  N25: C10.1, U6.XLAT1, XTAL3.pin_0
  N26: C11.0, U6.XLAT2, XTAL3.pin_1
  N27: C12.0, ICSP.pin1

notes:
  This is a stripboard Arduino without an FTDI chip. You can load sketches on the chip through the FTDI header (like the Lily Pad).
  http://arduino.cc/en/Guide/ArduinoLilyPad
  Angad uno
  ICSP
